// Logisim project 2-Logosim.circ as structural Verilog: 4 circuits, main circuit main
module main (
  input  R,
  input  A,
  input  B,
  input  S,
  input  A_2,
  input  B_2,
  output Y,
  output Y_2
);

  wire not_1_out, not_2_out;

  and and_1 (Y, A, B);
  not not_1 (not_1_out, A_2);
  not not_2 (not_2_out, B_2);
  or or_1 (Y_2, not_1_out, not_2_out);
  not not_3 (Y_2, Y);
  not not_4 (Y, Y_2);

  // Notes on the sheet:
  //   NAND
  //   AND
endmodule

module AND (
  input  A,
  input  B,
  output Y
);

  and and_1 (Y, A, B);
endmodule

module NAND (
  input  A,
  input  B,
  output Y
);

  wire not_1_out, not_2_out;

  not not_1 (not_1_out, A);
  not not_2 (not_2_out, B);
  or or_1 (Y, not_1_out, not_2_out);
endmodule

module RS (
  input  R,
  input  S,
  input  R_2,
  input  C,
  input  S_2,
  input  _1,
  input  _0,
  input  E,
  output out_9,
  output out_10,
  output Q,
  output nQ
);

  S_R_Flip_Flop s_r_ff_1 (.S(S_2), .clk(C), .R(R_2), .Q(Q), .Qn(nQ), .preset(_1), .reset(_0), .en(E));
  nor nor_1 (out_9, R, out_10);
  nor nor_2 (out_10, out_9, S);

  // Notes on the sheet:
  //   СХЕМА НЕ АВТОМАТ
  //   СХЕМА АВТОМАТ
endmodule
