// Logisim project 3-Logisim.circ as structural Verilog: 1 circuit, main circuit main
module main (
  input  \А ,
  input  \В ,
  input  Cin,
  output Count,
  output S
);

  wire and_1_out, and_2_out, xor_1_out;

  and and_1 (and_1_out, \А , \В );
  and and_2 (and_2_out, Cin, xor_1_out);
  or or_1 (Count, and_1_out, and_2_out);
  xor xor_1 (xor_1_out, \А , \В );
  xor xor_2 (S, xor_1_out, Cin);
endmodule
